// Digital circuit alu8bits.dig as structural Verilog
module alu8bits (
  input  [7:0] N,
  input  [2:0] S,
  input  CLK
);

  wire sMQ;
  wire [7:0] _000, _001, _010, _011, _100, _101, _110, _111, AC, MQ, MQ0, MQ1, multiplexer_1_out,
       multiplexer_2_out;

  Multiplexer #(.Bits(8)) multiplexer_1 (.sel(sMQ), .in_0(MQ0), .in_1(MQ1), .out(multiplexer_1_out));
  Register #(.Bits(8)) u_AC (.D(multiplexer_2_out), .C(CLK), .en(1'b1), .Q(AC));
  Register #(.Bits(8)) u_MQ (.D(multiplexer_1_out), .C(CLK), .en(1'b1), .Q(MQ));
  Multiplexer #(.Bits(8), .Selector_Bits(3)) multiplexer_2 (
    .sel(S), .in_0(_000), .in_1(_001), .in_2(_010), .in_3(_011), .in_4(_100), .in_5(_101), .in_6(_110),
    .in_7(_111), .out(multiplexer_2_out));
  and and_1 (sMQ, S[0], S[1], ~S[2]);  // And
  somador somador_1 ();  // open: AC, N, S, Overflow
  subtrator subtrator_1 ();  // open: AC, N, S, Overflow
  multiplicador multiplicador_1 ();  // open: AC, B, ACout, MQout
  divisor8bits divisor8bits_1 ();  // open: A, B, Q, Resto

  // Other names for the same wires on the sheet: sAC[2:0] = S
endmodule
