// Digital circuit cpu8bits.dig as structural Verilog
module cpu8bits (
);

  wire contador4bits_1_p1;

  // contador4bits contador4bits_1: pin names not known; wires that end beside it: contador4bits_1_p1, contador4bits_1_p1
  Driver driver_1 (.in(contador4bits_1_p1));  // open: en, out
  contador_de_anel4bits contador_de_anel4bits_1 ();  // open: CLK, Set, O0, O1, O2, O3
  alu8bits alu8bits_1 ();  // open: N, S, CLK, MQ, neg, AC, Over
endmodule
