// Digital circuit divisor8bits.dig as structural Verilog
module divisor8bits (
  input  B1,
  input  A3,
  input  B0,
  input  Q3
);

  wire subtrator1bit_1_cout, subtrator1bit_1_d, subtrator1bit_2_cout, subtrator1bit_2_d;

  not not_1 (Q3, subtrator1bit_1_cout);
  subtrator1bit subtrator1bit_1 (
    .A(B1), .B(1'b0), .Cin(subtrator1bit_2_cout), .D(subtrator1bit_1_d), .Cout(subtrator1bit_1_cout));
  Multiplexer multiplexer_1 (.sel(Q3), .in_0(1'b0), .in_1(subtrator1bit_1_d));  // open: out
  subtrator1bit subtrator1bit_2 (.A(B0), .B(A3), .Cin(1'b1), .D(subtrator1bit_2_d), .Cout(subtrator1bit_2_cout));
  Multiplexer multiplexer_2 (.sel(Q3), .in_0(A3), .in_1(subtrator1bit_2_d));  // open: out
endmodule
